# Fritzing sketch Galileo 1 (saved by Fritzing 0.9.2b)

parts:
  Parte1 = Arduino Uno (Rev3) - ICSP
  motorcontrollerDRI1 = motorcontrollerDRI0002
  BAT2 = Battery Holders [package=battery-aaa]
  BAT3 = Battery Holders [package=battery-aaa]
  BAT4 = Battery Holders [package=battery-aaa]
  BAT5 = Battery Holders [package=battery-aaa]
  BAT1 = Battery Holders [package=battery-aaa]
  M1 = DC Motor
  M2 = DC Motor
  M3 = DC Motor
  M4 = DC Motor

nets:
  GND: Parte1.GND, motorcontrollerDRI1.GND, BAT1.-
  N1: Parte1.D4, motorcontrollerDRI1.M1
  N2: Parte1.D5_PWM, motorcontrollerDRI1.E1
  N3: Parte1.D6_PWM, motorcontrollerDRI1.E2
  N4: Parte1.D7, motorcontrollerDRI1.M2
  N5: motorcontrollerDRI1.VS, BAT5.+
  N6: motorcontrollerDRI1.M1-, M3.pin_2, M4.pin_1
  N7: motorcontrollerDRI1.M1+, M3.pin_1, M4.pin_2
  N8: motorcontrollerDRI1.M2+, M1.pin_1, M2.pin_2
  N9: motorcontrollerDRI1.M2-, M1.pin_2, M2.pin_1
  N10: BAT2.-, BAT1.+
  N11: BAT2.+, BAT3.-
  N12: BAT3.+, BAT4.-
  N13: BAT4.+, BAT5.-

notes:
  Right Back Motor
  Right Front Motor
  Left Front Motor
  Left Back Motor
  - Motor green terminal is an anode.
  - Motor yellow terminal is a cathode.
